# Fritzing sketch breadboard (saved by Fritzing 0.9.4)
breadboards: 2

parts:
  Part2 = Arduino Motor Shield (Rev3)
  M2 = DC Motor
  M3 = DC Motor
  Mod1 = KY-019 5V Relay Module [package="Breakout board"]
  S1 = Limit Switch [package="Breakout Board"]
  S2 = Limit Switch [package="Breakout Board"]
  S3 = Limit Switch [package="Breakout Board"]
  S4 = Limit Switch [package="Breakout Board"]
  L1 = Solenoid
  D1 = Rectifier Diode [part_number=1N4001 package="300 mil [THT]"]
  J1 = 2.1mm Barrel Jack with Terminal Block

nets:
  N1: Part2.D10_PWM, Mod1.S
  N2: Part2.GND, Mod1.-, S1.G, S2.G, S3.G, S4.G
  N3: Part2.D4, S4.S
  N4: Part2.D5_PWM, S3.S
  N5: Part2.D6_PWM, S2.S
  N6: Part2.D7, S1.S
  N7: Part2.B-, M3.pin_2
  N8: Part2.B+, M3.pin_1
  N9: Part2.A-, M2.pin_2
  N10: Part2.A+, M2.pin_1
  N11: Part2.5V, Mod1.+
  N12: Mod1.Common, J1.NEG
  N13: Mod1.NO, L1.pin1, D1.anode
  N14: L1.pin2, D1.cathode, J1.POS

custom parts:
  KY-019 5V Relay Module: KY-019 5V Relay module, used to control AC circuits. (Special thanks to vanepp for fixing the PCB holes and other errors)
  Limit Switch: Generic limit switch commonly found on 3D printers. Typical lever microswitch mounted on a PCB board with a 3 pin JST XH connector.
